# Fritzing sketch Circuit (saved by Fritzing 1.0.1rc)
breadboards: 1

parts:
  Mod1 = Raspberry Pi Pico
  A1 = Waveshare 1.54in epaper display
  Q1 = NPN-Transistor [package="TO92 [THT]"]
  R1 = Resistor [tolerance=±5% power=0.25W resistance=10k package=THT]

nets:
  N1: Mod1.pin_1, R1.Pin_1
  N2: Mod1.pin_3, Mod1.pin_8, Mod1.pin_13, Mod1.pin_18, Mod1.pin_23, Mod1.pin_28, Mod1.pin_33, Mod1.pin_38, Mod1.pin_42, Q1.E
  N3: Mod1.pin_11, A1.Pin_3
  N4: Mod1.pin_12, A1.Pin_4
  N5: Mod1.pin_14, A1.Pin_5
  N6: Mod1.pin_15, A1.Pin_6
  N7: Mod1.pin_16, A1.Pin_2
  N8: Mod1.pin_17, A1.Pin_1
  N9: Mod1.pin_36, A1.Pin_8
  N10: A1.Pin_7, Q1.C
  N11: Q1.B, R1.Pin_0

custom parts:
  Raspberry Pi Pico: Raspberry Pi Pico. Based around the RP2040 microcontroller the Pico is a low cost microcontroller device bringing Raspberry Pi quality, cost, and easy of use to the microcontroller space. Jan 2021, Split part in to two versions: tht (this one) and SMD. This one will drill holes for a .1 in header in pcb to allow plugging in the module as well as providing pads to solder the module to the top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
  Waveshare 1.54in epaper display: This is an E-Ink display module, 1.54inch, 200x200 resolution, with embedded controller, communicating via SPI interface.
